// Logisim project DigitalClock.circ as structural Verilog: 8 circuits, main circuit main
module main (
);

  wire binary_to_7_seg_decoder_1_qa, binary_to_7_seg_decoder_1_qb, binary_to_7_seg_decoder_1_qc,
       binary_to_7_seg_decoder_1_qd, binary_to_7_seg_decoder_1_qe, binary_to_7_seg_decoder_1_qf,
       binary_to_7_seg_decoder_1_qg, binary_to_7_seg_decoder_2_qa, binary_to_7_seg_decoder_2_qb,
       binary_to_7_seg_decoder_2_qc, binary_to_7_seg_decoder_2_qd, binary_to_7_seg_decoder_2_qe,
       binary_to_7_seg_decoder_2_qf, binary_to_7_seg_decoder_2_qg, binary_to_7_seg_decoder_3_qa,
       binary_to_7_seg_decoder_3_qb, binary_to_7_seg_decoder_3_qc, binary_to_7_seg_decoder_3_qd,
       binary_to_7_seg_decoder_3_qe, binary_to_7_seg_decoder_3_qf, binary_to_7_seg_decoder_3_qg,
       binary_to_7_seg_decoder_4_qa, binary_to_7_seg_decoder_4_qb, binary_to_7_seg_decoder_4_qc,
       binary_to_7_seg_decoder_4_qd, binary_to_7_seg_decoder_4_qe, binary_to_7_seg_decoder_4_qf,
       binary_to_7_seg_decoder_4_qg, Clock_out, hour_decoder_1_qa0, hour_decoder_1_qa1, hour_decoder_1_qb0,
       hour_decoder_1_qb1, hour_decoder_1_qc0, hour_decoder_1_qc1, hour_decoder_1_qd0, hour_decoder_1_qd1,
       hour_decoder_1_qe0, hour_decoder_1_qe1, hour_decoder_1_qf0, hour_decoder_1_qf1, hour_decoder_1_qg0,
       hour_decoder_1_qg1, n0_5_counter_1_clk_out, n0_5_counter_1_q0, n0_5_counter_1_q1, n0_5_counter_1_q2,
       n0_5_counter_2_clk_out, n0_5_counter_2_q0, n0_5_counter_2_q1, n0_5_counter_2_q2,
       n0_9_counter_1_clk_out, n0_9_counter_1_q0, n0_9_counter_1_q1, n0_9_counter_1_q2, n0_9_counter_1_q3,
       n0_9_counter_2_clk_out, n0_9_counter_2_q0, n0_9_counter_2_q1, n0_9_counter_2_q2, n0_9_counter_2_q3,
       n1_12_counter_1_am___pm_toggle, n1_12_counter_1_q0, n1_12_counter_1_q1, n1_12_counter_1_q2,
       n1_12_counter_1_q3, Set_Hour_out, Set_Minute_out, Set_Seconds_out, xor_1_out, xor_2_out, xor_3_out;

  LED PM (.in(n1_12_counter_1_am___pm_toggle));
  _7_Segment_Display u_7_segment_display_1 (
    .g(hour_decoder_1_qg0), .f(hour_decoder_1_qf0), .a(hour_decoder_1_qa0), .b(hour_decoder_1_qb0),
    .e(hour_decoder_1_qe0), .d(hour_decoder_1_qd0), .c(hour_decoder_1_qc0));  // open: dp
  Hour_Decoder hour_decoder_1 (
    .QA0(hour_decoder_1_qa0), .QB0(hour_decoder_1_qb0), .QC0(hour_decoder_1_qc0), .QD0(hour_decoder_1_qd0),
    .QE0(hour_decoder_1_qe0), .QF0(hour_decoder_1_qf0), .QG0(hour_decoder_1_qg0), .QA1(hour_decoder_1_qa1),
    .QB1(hour_decoder_1_qb1), .QC1(hour_decoder_1_qc1), .QD1(hour_decoder_1_qd1), .QE1(hour_decoder_1_qe1),
    .QF1(hour_decoder_1_qf1), .QG1(hour_decoder_1_qg1), .I3(n1_12_counter_1_q3), .I2(n1_12_counter_1_q2),
    .I1(n1_12_counter_1_q1), .I0(n1_12_counter_1_q0));
  _7_Segment_Display u_7_segment_display_2 (
    .g(hour_decoder_1_qg1), .f(hour_decoder_1_qf1), .a(hour_decoder_1_qa1), .b(hour_decoder_1_qb1),
    .e(hour_decoder_1_qe1), .d(hour_decoder_1_qd1), .c(hour_decoder_1_qc1));  // open: dp
  _1_12_Counter u_1_12_counter_1 (
    .AM___PM_Toggle(n1_12_counter_1_am___pm_toggle), .Q3(n1_12_counter_1_q3), .Q2(n1_12_counter_1_q2),
    .Q1(n1_12_counter_1_q1), .Q0(n1_12_counter_1_q0), .Clk_In(xor_1_out));
  xor xor_1 (xor_1_out, n0_5_counter_1_clk_out, Set_Hour_out);
  _7_Segment_Display u_7_segment_display_3 (
    .g(binary_to_7_seg_decoder_1_qg), .f(binary_to_7_seg_decoder_1_qf), .a(binary_to_7_seg_decoder_1_qa),
    .b(binary_to_7_seg_decoder_1_qb), .e(binary_to_7_seg_decoder_1_qe), .d(binary_to_7_seg_decoder_1_qd),
    .c(binary_to_7_seg_decoder_1_qc));  // open: dp
  Binary_to_7_Seg_Decoder binary_to_7_seg_decoder_1 (
    .QA(binary_to_7_seg_decoder_1_qa), .QB(binary_to_7_seg_decoder_1_qb), .QC(binary_to_7_seg_decoder_1_qc),
    .QD(binary_to_7_seg_decoder_1_qd), .QE(binary_to_7_seg_decoder_1_qe), .QF(binary_to_7_seg_decoder_1_qf),
    .QG(binary_to_7_seg_decoder_1_qg), .I3(1'b0), .I2(n0_5_counter_1_q2), .I1(n0_5_counter_1_q1),
    .I0(n0_5_counter_1_q0));
  Button Set_Hour (.out(Set_Hour_out));
  _7_Segment_Display u_7_segment_display_4 (
    .g(binary_to_7_seg_decoder_2_qg), .f(binary_to_7_seg_decoder_2_qf), .a(binary_to_7_seg_decoder_2_qa),
    .b(binary_to_7_seg_decoder_2_qb), .e(binary_to_7_seg_decoder_2_qe), .d(binary_to_7_seg_decoder_2_qd),
    .c(binary_to_7_seg_decoder_2_qc));  // open: dp
  Binary_to_7_Seg_Decoder binary_to_7_seg_decoder_2 (
    .QA(binary_to_7_seg_decoder_2_qa), .QB(binary_to_7_seg_decoder_2_qb), .QC(binary_to_7_seg_decoder_2_qc),
    .QD(binary_to_7_seg_decoder_2_qd), .QE(binary_to_7_seg_decoder_2_qe), .QF(binary_to_7_seg_decoder_2_qf),
    .QG(binary_to_7_seg_decoder_2_qg), .I3(n0_9_counter_1_q3), .I2(n0_9_counter_1_q2),
    .I1(n0_9_counter_1_q1), .I0(n0_9_counter_1_q0));
  _0_5_Counter u_0_5_counter_1 (
    .Clk_Out(n0_5_counter_1_clk_out), .Q2(n0_5_counter_1_q2), .Q1(n0_5_counter_1_q1), .Q0(n0_5_counter_1_q0),
    .Clk_In(n0_9_counter_1_clk_out));
  _0_9_Counter u_0_9_counter_1 (
    .Clk_Out(n0_9_counter_1_clk_out), .Q3(n0_9_counter_1_q3), .Q2(n0_9_counter_1_q2), .Q1(n0_9_counter_1_q1),
    .Q0(n0_9_counter_1_q0), .Clk_In(xor_2_out));
  xor xor_2 (xor_2_out, n0_5_counter_2_clk_out, Set_Minute_out);
  Button Set_Minute (.out(Set_Minute_out));
  _7_Segment_Display u_7_segment_display_5 (
    .g(binary_to_7_seg_decoder_3_qg), .f(binary_to_7_seg_decoder_3_qf), .a(binary_to_7_seg_decoder_3_qa),
    .b(binary_to_7_seg_decoder_3_qb), .e(binary_to_7_seg_decoder_3_qe), .d(binary_to_7_seg_decoder_3_qd),
    .c(binary_to_7_seg_decoder_3_qc));  // open: dp
  Binary_to_7_Seg_Decoder binary_to_7_seg_decoder_3 (
    .QA(binary_to_7_seg_decoder_3_qa), .QB(binary_to_7_seg_decoder_3_qb), .QC(binary_to_7_seg_decoder_3_qc),
    .QD(binary_to_7_seg_decoder_3_qd), .QE(binary_to_7_seg_decoder_3_qe), .QF(binary_to_7_seg_decoder_3_qf),
    .QG(binary_to_7_seg_decoder_3_qg), .I3(1'b0), .I2(n0_5_counter_2_q2), .I1(n0_5_counter_2_q1),
    .I0(n0_5_counter_2_q0));
  _0_5_Counter u_0_5_counter_2 (
    .Clk_Out(n0_5_counter_2_clk_out), .Q2(n0_5_counter_2_q2), .Q1(n0_5_counter_2_q1), .Q0(n0_5_counter_2_q0),
    .Clk_In(n0_9_counter_2_clk_out));
  _7_Segment_Display u_7_segment_display_6 (
    .g(binary_to_7_seg_decoder_4_qg), .f(binary_to_7_seg_decoder_4_qf), .a(binary_to_7_seg_decoder_4_qa),
    .b(binary_to_7_seg_decoder_4_qb), .e(binary_to_7_seg_decoder_4_qe), .d(binary_to_7_seg_decoder_4_qd),
    .c(binary_to_7_seg_decoder_4_qc));  // open: dp
  Binary_to_7_Seg_Decoder binary_to_7_seg_decoder_4 (
    .QA(binary_to_7_seg_decoder_4_qa), .QB(binary_to_7_seg_decoder_4_qb), .QC(binary_to_7_seg_decoder_4_qc),
    .QD(binary_to_7_seg_decoder_4_qd), .QE(binary_to_7_seg_decoder_4_qe), .QF(binary_to_7_seg_decoder_4_qf),
    .QG(binary_to_7_seg_decoder_4_qg), .I3(n0_9_counter_2_q3), .I2(n0_9_counter_2_q2),
    .I1(n0_9_counter_2_q1), .I0(n0_9_counter_2_q0));
  xor xor_3 (xor_3_out, Clock_out, Set_Seconds_out);
  _0_9_Counter u_0_9_counter_2 (
    .Clk_Out(n0_9_counter_2_clk_out), .Q3(n0_9_counter_2_q3), .Q2(n0_9_counter_2_q2), .Q1(n0_9_counter_2_q1),
    .Q0(n0_9_counter_2_q0), .Clk_In(xor_3_out));
  Button Set_Seconds (.out(Set_Seconds_out));
  Clock_part Clock (.out(Clock_out));

  // Notes on the sheet:
  //   HOURS
  //   AKASH BHAT 
  //   DDCO MINI PROJECT
  //   ABHISHEK SASEENDRAN
  //   MINUTES
  //   ADITYA PANDEY
  //   SECONDS
endmodule

module _0_9_Counter (
  input  Clk_In,
  output Q3,
  output Q2,
  output Q1,
  output Q0,
  output Clk_Out
);

  wire and_2_out, and_3_out, and_4_out, and_5_out, or_1_out, t_ff_1_qn, t_ff_2_qn, t_ff_3_qn, t_ff_4_qn;

  and and_1 (Clk_Out, t_ff_1_qn, t_ff_2_qn, t_ff_3_qn, t_ff_4_qn);
  or or_1 (or_1_out, and_2_out, and_3_out);
  and and_2 (and_2_out, Q0, Q1, Q2);
  T_Flip_Flop t_ff_1 (.clk(Clk_In), .T(or_1_out), .Q(Q3), .Qn(t_ff_1_qn));  // open: preset, reset, en
  and and_3 (and_3_out, Q0, Q3);
  and and_4 (and_4_out, Q0, Q1);
  T_Flip_Flop t_ff_2 (.clk(Clk_In), .T(and_4_out), .Q(Q2), .Qn(t_ff_2_qn));  // open: preset, reset, en
  and and_5 (and_5_out, t_ff_1_qn, Q0);
  T_Flip_Flop t_ff_3 (.clk(Clk_In), .T(and_5_out), .Q(Q1), .Qn(t_ff_3_qn));  // open: preset, reset, en
  T_Flip_Flop t_ff_4 (.clk(Clk_In), .T(1'b1), .Q(Q0), .Qn(t_ff_4_qn));  // open: preset, reset, en
endmodule

module _0_5_Counter (
  input  Clk_In,
  output Q2,
  output Q1,
  output Q0,
  output Clk_Out
);

  wire and_2_out, and_3_out, or_1_out, t_ff_1_qn, t_ff_2_qn, t_ff_3_qn;

  and and_1 (Clk_Out, t_ff_1_qn, t_ff_2_qn, t_ff_3_qn);
  and and_2 (and_2_out, or_1_out, Q0);
  or or_1 (or_1_out, Q1, Q2);
  T_Flip_Flop t_ff_1 (.clk(Clk_In), .T(and_2_out), .Q(Q2), .Qn(t_ff_1_qn));  // open: preset, reset, en
  T_Flip_Flop t_ff_2 (.clk(Clk_In), .T(and_3_out), .Q(Q1), .Qn(t_ff_2_qn));  // open: preset, reset, en
  and and_3 (and_3_out, t_ff_1_qn, Q0);
  T_Flip_Flop t_ff_3 (.clk(Clk_In), .T(1'b1), .Q(Q0), .Qn(t_ff_3_qn));  // open: preset, reset, en
endmodule

// Decoder
module Binary_to_7_Seg_Decoder (
  input  I3,
  input  I2,
  input  I1,
  input  I0,
  output QA,
  output QB,
  output QC,
  output QD,
  output QE,
  output QF,
  output QG
);

  wire and_1_out, and_2_out, and_3_out, and_4_out, and_5_out, and_6_out, and_7_out, and_8_out, and_9_out,
       and_10_out, and_11_out, not_1_out, not_2_out, not_3_out, not_4_out, or_1_out, or_2_out, or_3_out,
       or_4_out;

  not not_1 (not_1_out, I3);
  not not_2 (not_2_out, I2);
  not not_3 (not_3_out, I1);
  not not_4 (not_4_out, I0);
  and and_1 (and_1_out, I2, I0);
  and and_2 (and_2_out, not_2_out, not_4_out);
  and and_3 (and_3_out, I1, I0);
  and and_4 (and_4_out, not_3_out, not_4_out);
  or or_1 (or_1_out, I1, not_2_out);
  and and_5 (and_5_out, or_1_out, not_4_out);
  and and_6 (and_6_out, I0, not_3_out, I2);
  and and_7 (and_7_out, I1, not_2_out);
  or or_2 (or_2_out, I1, not_2_out);
  or or_3 (or_3_out, not_4_out, not_3_out);
  and and_8 (and_8_out, or_3_out, I2);
  and and_9 (and_9_out, not_4_out, not_3_out);
  or or_4 (or_4_out, not_4_out, not_3_out);
  and and_10 (and_10_out, or_4_out, I2);
  and and_11 (and_11_out, I1, not_2_out);
  or or_5 (QA, and_1_out, and_2_out, I3, I1);
  or or_6 (QB, and_3_out, and_4_out, not_2_out);
  or or_7 (QC, I2, not_3_out, I0);
  or or_8 (QD, and_5_out, and_6_out, and_7_out, I3);
  and and_12 (QE, not_4_out, or_2_out);
  or or_9 (QF, and_8_out, and_9_out, I3);
  or or_10 (QG, and_10_out, and_11_out, I3);
endmodule

module _1_12_Counter (
  input  Clk_In,
  output Q3,
  output Q2,
  output Q1,
  output Q0,
  output AM___PM_Toggle
);

  wire and_1_out, and_2_out, and_3_out, and_4_out, button_1_out, t_ff_4_qn;

  T_Flip_Flop t_ff_1 (.clk(and_2_out), .T(1'b1), .Q(AM___PM_Toggle));  // open: Qn, preset, reset, en
  T_Flip_Flop t_ff_2 (.clk(Clk_In), .T(and_1_out), .Q(Q3), .reset(and_4_out));  // open: Qn, preset, en
  and and_1 (and_1_out, Q0, Q1, Q2);
  and and_2 (and_2_out, Q3, Q2);
  and and_3 (and_3_out, Q1, Q0);
  T_Flip_Flop t_ff_3 (.clk(Clk_In), .T(and_3_out), .Q(Q2), .reset(and_4_out));  // open: Qn, preset, en
  and and_4 (and_4_out, Q2, Q3, Q0, t_ff_4_qn);
  T_Flip_Flop t_ff_4 (.clk(Clk_In), .T(Q0), .Q(Q1), .Qn(t_ff_4_qn), .reset(and_4_out));  // open: preset, en
  T_Flip_Flop t_ff_5 (.clk(Clk_In), .T(1'b1), .Q(Q0), .preset(and_4_out));  // open: Qn, reset, en
  Button button_1 (.out(button_1_out));
endmodule

// Decoder
module Hour_Decoder (
  input  I3,
  input  I2,
  input  I1,
  input  I0,
  output QA0,
  output QB0,
  output QC0,
  output QA1,
  output QB1,
  output QC1,
  output QD1,
  output QD0,
  output QE1,
  output QF1,
  output QG1,
  output QE0,
  output QF0,
  output QG0
);

  wire and_8_out, not_1_out, not_2_out, not_3_out, not_4_out, or_1_out, or_2_out, or_3_out, or_4_out,
       or_5_out, or_6_out, or_7_out, or_8_out, or_9_out, or_10_out, or_11_out, or_12_out, or_13_out,
       or_14_out, or_15_out, or_16_out, or_17_out, or_18_out, or_19_out;

  not not_1 (not_1_out, I3);
  not not_2 (not_2_out, I1);
  not not_3 (not_3_out, I0);
  not not_4 (not_4_out, I2);
  or or_1 (or_1_out, not_3_out, not_2_out, not_1_out);
  or or_2 (or_2_out, I0, I1, not_4_out, I3);
  or or_3 (or_3_out, not_3_out, I1, I2, I3);
  or or_4 (or_4_out, I0, not_2_out, not_4_out);
  and and_1 (QB0, or_4_out, or_5_out);
  or or_5 (or_5_out, not_3_out, I1, not_4_out);
  or or_6 (or_6_out, not_4_out, not_1_out);
  or or_7 (or_7_out, I0, not_2_out, I2, I3);
  or or_8 (or_8_out, not_3_out, not_1_out);
  or or_9 (or_9_out, not_3_out, not_2_out, not_4_out);
  or or_10 (or_10_out, not_3_out, I1, I2);
  or or_11 (or_11_out, I0, I1, not_4_out, I3);
  or or_12 (or_12_out, I1, not_4_out, I3);
  or or_13 (or_13_out, not_4_out, not_1_out);
  or or_14 (or_14_out, not_3_out, not_2_out);
  or or_15 (or_15_out, not_2_out, I2, I3);
  or or_16 (or_16_out, not_3_out, I2, I3);
  or or_17 (or_17_out, not_2_out, not_1_out);
  or or_18 (or_18_out, not_3_out, not_2_out, not_4_out);
  and and_2 (QG0, or_17_out, or_18_out, or_19_out);
  or or_19 (or_19_out, I1, I2, I3);
  and and_3 (QA0, or_1_out, or_2_out, or_3_out);
  and and_4 (QC0, or_6_out, or_7_out);
  and and_5 (QD0, or_8_out, or_9_out, or_10_out, or_11_out);
  and and_6 (QE0, not_3_out, or_12_out);
  and and_7 (QF0, or_13_out, or_14_out, or_15_out, or_16_out);
  and and_8 (and_8_out, not_2_out, not_4_out);
  or or_20 (QA1, not_1_out, and_8_out);

  assign QB1 = 1'b1;
  assign QC1 = 1'b1;
  assign QD1 = QA1;
  assign QE1 = QA1;
  assign QF1 = QA1;
  assign QG1 = 1'b0;
endmodule

// Comparator
module _12_bit_Comparator (
  input  A11,
  input  A10,
  input  A9,
  input  A8,
  input  A7,
  input  A6,
  input  A5,
  input  A4,
  input  A3,
  input  A3_2,
  input  A1,
  input  A0,
  input  B11,
  input  B10,
  input  B9,
  input  B8,
  input  B7,
  input  B6,
  input  B5,
  input  B4,
  input  B3,
  input  B3_2,
  input  B1,
  input  B0,
  output out_25
);

  wire xnor_1_out, xnor_2_out, xnor_3_out, xnor_4_out, xnor_5_out, xnor_6_out, xnor_7_out, xnor_8_out,
       xnor_9_out, xnor_10_out, xnor_11_out, xnor_12_out;

  xnor xnor_1 (xnor_1_out, B0, A0);
  xnor xnor_2 (xnor_2_out, B1, A1);
  xnor xnor_3 (xnor_3_out, B3_2, A3_2);
  xnor xnor_4 (xnor_4_out, B3, A3);
  xnor xnor_5 (xnor_5_out, B4, A4);
  xnor xnor_6 (xnor_6_out, B5, A5);
  xnor xnor_7 (xnor_7_out, B6, A6);
  xnor xnor_8 (xnor_8_out, B7, A7);
  xnor xnor_9 (xnor_9_out, B8, A8);
  xnor xnor_10 (xnor_10_out, B9, A9);
  xnor xnor_11 (xnor_11_out, B10, A10);
  xnor xnor_12 (xnor_12_out, B11, A11);
  and and_1 (out_25, xnor_1_out, xnor_2_out, xnor_3_out, xnor_4_out, xnor_5_out, xnor_6_out, xnor_7_out, xnor_8_out, xnor_9_out, xnor_10_out, xnor_11_out, xnor_12_out);
endmodule

module Clock (
  input  Clk_In,
  input  Set_Hour,
  input  Set_Minute,
  output [11:0] out_4
);

  wire n0_5_counter_1_clk_out, n0_9_counter_1_clk_out, n1_12_counter_1_am___pm_toggle, xor_1_out, xor_2_out;

  T_Flip_Flop t_ff_1 (.clk(n1_12_counter_1_am___pm_toggle), .T(1'b1), .Q(out_4[11]));  // open: Qn, preset, reset, en
  _1_12_Counter u_1_12_counter_1 (
    .AM___PM_Toggle(n1_12_counter_1_am___pm_toggle), .Q3(out_4[10]), .Q2(out_4[9]), .Q1(out_4[8]),
    .Q0(out_4[8]), .Clk_In(xor_1_out));
  xor xor_1 (xor_1_out, n0_5_counter_1_clk_out, Set_Hour);
  _0_5_Counter u_0_5_counter_1 (
    .Clk_Out(n0_5_counter_1_clk_out), .Q2(out_4[6]), .Q1(out_4[5]), .Q0(out_4[4]),
    .Clk_In(n0_9_counter_1_clk_out));
  xor xor_2 (xor_2_out, Clk_In, Set_Minute);
  _0_9_Counter u_0_9_counter_1 (
    .Clk_Out(n0_9_counter_1_clk_out), .Q3(out_4[3]), .Q2(out_4[2]), .Q1(out_4[1]), .Q0(out_4[0]),
    .Clk_In(xor_2_out));

  assign out_4[7] = out_4[8];
endmodule
